# Fritzing sketch mobile_base_circuit (saved by Fritzing 1.0.3b)
breadboards: 1

parts:
  M1 = Stepper Motor - Bipolar -17HS8401
  A1 = Arduino UNO R4 WiFi
  A2 = Raspberry Pi 5  # not connected
  DRV_1 = DRV 8825 Stepper Motor Carrier, High Current [part_number="DRV 8825"]
  Power_plug1 = Power plug
  C1 = Electrolytic Capacitor [capacitance=100μF voltage=35V package="0807 [SMD, electrolytic]"]
  DRV_2 = DRV 8825 Stepper Motor Carrier, High Current [part_number="DRV 8825"]
  M2 = Stepper Motor - Bipolar -17HS8401

nets:
  N1: M1.A, DRV_1.OUT_2B
  N2: M1.C, DRV_1.OUT_2A
  N3: M1.B, DRV_1.OUT_1A
  N4: M1.D, DRV_1.OUT_1B
  100 μA draw each logic pin high/500mA max: A1.Pin_8, DRV_1.RESET, DRV_1.SLEEP, DRV_2.RESET, DRV_2.SLEEP
  N5: A1.Pin_9, A1.Pin_18, DRV_1.GROUND_LOG, DRV_2.GROUND_LOG
  N6: A1.Pin_36, DRV_1.DIRECTION
  N7: A1.Pin_37, DRV_1.STEP
  N8: A1.Pin_38, DRV_2.DIRECTION
  N9: A1.Pin_39, DRV_2.STEP
  N10: DRV_1.VOLTAGE_ST/_MT, Power_plug1.VCC, C1.-, DRV_2.VOLTAGE_ST/_MT
  N11: DRV_1.GROUND_ST/_MT, Power_plug1.GND, C1.+, DRV_2.GROUND_ST/_MT
  N12: DRV_2.OUT_2B, M2.A
  N13: DRV_2.OUT_2A, M2.C
  N14: DRV_2.OUT_1A, M2.B
  N15: DRV_2.OUT_1B, M2.D

custom parts:
  Stepper Motor - Bipolar -17HS8401: Simple, but very powerful bi polar stepper motor. 4 wire
  Arduino UNO R4 WiFi: The Arduino UNO R4 WiFi merges the RA4M1 microprocessor from Renesas with the ESP32-S3 from Espressif, creating an all-in-one tool for makers with enhanced processing power and a diverse array of new peripherals.
  Raspberry Pi 5: The RPi5, a faster version of the awesome Raspberry Pi4B ARM Board with 40 pin gpio.
